// Digital circuit part_a.dig as structural Verilog
module part_a (
  input  in_0,
  input  in_2,
  input  in_1,
  output out_0
);

  wire not_1_out, xnor_1_out;

  not not_1 (not_1_out, in_1);
  xnor xnor_1 (xnor_1_out, in_0, in_2);
  or or_1 (out_0, xnor_1_out, not_1_out);
endmodule

/* Test case part_a_test:
in_0 in_1 in_2 out_0
0 0 0 1
0 0 1 1 
0 1 0 1
0 1 1 0
1 0 0 1
1 0 1 1
1 1 0 0
1 1 1 1
*/
