// Digital circuit lab2_part1_v2.dig as structural Verilog
module lab2_part1_v2 (
  input  inA_0,
  input  inA_1,
  input  inA_2,
  input  inA_3,
  input  inB_0,
  input  inB_1,
  input  inB_2,
  input  inB_3,
  output out0,
  output out1,
  output out2,
  output out3
);

  wire and_1_out, and_2_out, and_3_out, and_4_out, and_5_out, and_6_out, and_7_out, and_8_out, and_9_out,
       and_10_out, and_11_out, and_12_out, and_13_out, and_14_out, and_15_out, and_16_out;

  and and_1 (and_1_out, ~inB_1, ~inB_0, inA_3);  // And
  and and_2 (and_2_out, inB_1, inB_0, inA_2);
  and and_3 (and_3_out, inB_1, ~inB_0, inA_1);  // And
  and and_4 (and_4_out, ~inB_1, inB_0, inA_0);  // And
  and and_5 (and_5_out, ~inB_1, inB_0, inA_3);  // And
  and and_6 (and_6_out, ~inB_1, ~inB_0, inA_2);  // And
  and and_7 (and_7_out, inB_1, inB_0, inA_1);
  and and_8 (and_8_out, inB_1, ~inB_0, inA_0);  // And
  and and_9 (and_9_out, inB_1, ~inB_0, inA_3);  // And
  and and_10 (and_10_out, ~inB_1, inB_0, inA_2);  // And
  and and_11 (and_11_out, ~inB_1, ~inB_0, inA_1);  // And
  and and_12 (and_12_out, inB_1, inB_0, inA_0);
  and and_13 (and_13_out, inB_1, inB_0, inA_3);
  and and_14 (and_14_out, inB_1, ~inB_0, inA_2);  // And
  and and_15 (and_15_out, ~inB_1, inB_0, inA_1);  // And
  and and_16 (and_16_out, ~inB_1, ~inB_0, inA_0);  // And
  or or_1 (out3, and_1_out, and_2_out, and_3_out, and_4_out);
  or or_2 (out2, and_5_out, and_6_out, and_7_out, and_8_out);
  or or_3 (out1, and_9_out, and_10_out, and_11_out, and_12_out);
  or or_4 (out0, and_13_out, and_14_out, and_15_out, and_16_out);

  // Notes on the sheet:
  //   Interface (do not edit the content inside this box)
  //   Inputs
  //   Outputs
  //   Rotatee:
  //   Rotation amount:
  //   Result of Rotating  input A by the amount given by input B:
endmodule

/* Test case:
inA_3 inA_2 inA_1 inA_0 inB_1 inB_0  out3 out2 out1 out0
 0     0     0     0     0     0      0    0    0    0  
 0     0     0     1     0     0      0    0    0    1  
 0     0     0     1     0     1      1    0    0    0  
 0     0     0     1     1     0      0    1    0    0  
 0     0     0     1     1     1      0    0    1    0   
 0     1     0     1     0     0      0    1    0    1  
 0     1     0     1     0     1      1    0    1    0  
 0     1     0     1     1     0      0    1    0    1  
 0     1     0     1     1     1      1    0    1    0  
*/
