// Digital circuit lab2_part2.dig as structural Verilog
module lab2_part2 (
  input  in0,
  input  in1,
  input  in2,
  input  in3,
  output seg_a,
  output seg_f,
  output seg_b,
  output seg_g,
  output seg_e,
  output seg_c,
  output seg_d,
  output seg_dp,
  output sign_a,
  output sign_f,
  output sign_b,
  output sign_g,
  output sign_e,
  output sign_c,
  output sign_d,
  output sign_dp
);

  wire and_1_out, and_2_out, and_3_out, and_4_out, and_5_out, and_6_out, and_7_out, and_8_out, and_9_out,
       and_10_out, and_11_out, and_12_out, and_13_out, and_14_out, and_15_out, and_16_out, and_17_out,
       and_18_out, and_19_out, and_20_out, and_21_out, and_22_out, and_23_out, and_24_out, and_25_out,
       and_26_out, and_27_out, and_28_out, and_29_out, and_30_out, and_31_out, and_32_out, and_33_out,
       and_34_out, and_35_out, and_36_out, and_37_out, and_38_out, and_39_out, and_40_out, and_41_out,
       and_42_out, and_43_out, and_44_out, and_45_out, and_46_out, and_47_out, and_48_out, and_49_out,
       and_50_out, and_51_out, and_52_out, and_53_out, and_54_out, and_55_out, and_56_out, and_57_out,
       and_58_out, and_59_out, and_60_out, and_61_out, and_62_out, and_63_out, and_64_out, and_65_out,
       and_66_out, and_67_out, and_68_out, and_69_out, and_70_out, and_71_out, and_72_out, and_73_out;

  and and_1 (and_1_out, ~in3, ~in2, in1, ~in0);  // And
  and and_2 (and_2_out, ~in3, ~in2, in1, in0);  // And
  and and_3 (and_3_out, ~in3, in2, ~in1, ~in0);  // And
  and and_4 (and_4_out, ~in3, in2, ~in1, in0);  // And
  and and_5 (and_5_out, ~in3, in2, in1, ~in0);  // And
  and and_6 (and_6_out, in3, ~in2, ~in1, in0);  // And
  and and_7 (and_7_out, in3, ~in2, in1, ~in0);  // And
  and and_8 (and_8_out, in3, ~in2, in1, in0);  // And
  and and_9 (and_9_out, in3, in2, ~in1, ~in0);  // And
  and and_10 (and_10_out, in3, in2, ~in1, in0);  // And
  and and_11 (and_11_out, in3, in2, in1, in0);
  or or_1 (seg_g, and_6_out, and_1_out, and_7_out, and_2_out, and_8_out, and_3_out, and_9_out, and_4_out, and_10_out, and_5_out, and_11_out);
  and and_12 (and_12_out, ~in3, ~in2, ~in1, ~in0);  // And
  and and_13 (and_13_out, ~in3, in2, ~in1, ~in0);  // And
  and and_14 (and_14_out, ~in3, in2, ~in1, in0);  // And
  and and_15 (and_15_out, ~in3, in2, in1, ~in0);  // And
  and and_16 (and_16_out, in3, ~in2, in1, in0);  // And
  and and_17 (and_17_out, in3, in2, ~in1, ~in0);  // And
  and and_18 (and_18_out, in3, in2, ~in1, in0);  // And
  and and_19 (and_19_out, in3, in2, in1, in0);
  or or_2 (seg_f, and_12_out, and_16_out, and_13_out, and_17_out, and_14_out, and_18_out, and_15_out, and_19_out);
  and and_20 (and_20_out, ~in3, ~in2, ~in1, ~in0);  // And
  and and_21 (and_21_out, ~in3, ~in2, in1, ~in0);  // And
  and and_22 (and_22_out, ~in3, in2, in1, ~in0);  // And
  and and_23 (and_23_out, in3, ~in2, ~in1, in0);  // And
  and and_24 (and_24_out, in3, in2, ~in1, in0);  // And
  and and_25 (and_25_out, in3, in2, in1, in0);
  or or_3 (seg_e, and_20_out, and_23_out, and_21_out, and_24_out, and_22_out, and_25_out);
  and and_26 (and_26_out, ~in3, ~in2, ~in1, ~in0);  // And
  and and_27 (and_27_out, ~in3, ~in2, in1, ~in0);  // And
  and and_28 (and_28_out, ~in3, ~in2, in1, in0);  // And
  and and_29 (and_29_out, ~in3, in2, ~in1, in0);  // And
  and and_30 (and_30_out, ~in3, in2, in1, ~in0);  // And
  and and_31 (and_31_out, in3, ~in2, ~in1, in0);  // And
  and and_32 (and_32_out, in3, ~in2, in1, ~in0);  // And
  and and_33 (and_33_out, in3, in2, ~in1, ~in0);  // And
  and and_34 (and_34_out, in3, in2, ~in1, in0);  // And
  and and_35 (and_35_out, in3, in2, in1, in0);
  or or_4 (seg_d, and_26_out, and_31_out, and_27_out, and_32_out, and_28_out, and_33_out, and_29_out, and_34_out, and_30_out, and_35_out);
  and and_36 (and_36_out, ~in3, ~in2, ~in1, ~in0);  // And
  and and_37 (and_37_out, ~in3, ~in2, ~in1, in0);  // And
  and and_38 (and_38_out, ~in3, ~in2, in1, in0);  // And
  and and_39 (and_39_out, ~in3, in2, ~in1, ~in0);  // And
  and and_40 (and_40_out, ~in3, in2, ~in1, in0);  // And
  and and_41 (and_41_out, ~in3, in2, in1, ~in0);  // And
  and and_42 (and_42_out, ~in3, in2, in1, in0);  // And
  and and_43 (and_43_out, in3, ~in2, ~in1, ~in0);  // And
  and and_44 (and_44_out, in3, ~in2, in1, ~in0);  // And
  and and_45 (and_45_out, in3, ~in2, in1, in0);  // And
  and and_46 (and_46_out, in3, in2, ~in1, ~in0);  // And
  and and_47 (and_47_out, in3, in2, ~in1, in0);  // And
  and and_48 (and_48_out, in3, in2, in1, ~in0);  // And
  and and_49 (and_49_out, in3, in2, in1, in0);
  or or_5 (seg_c, and_36_out, and_43_out, and_37_out, and_44_out, and_38_out, and_45_out, and_39_out, and_46_out, and_40_out, and_47_out, and_41_out, and_48_out, and_42_out, and_49_out);
  and and_50 (and_50_out, ~in3, ~in2, ~in1, ~in0);  // And
  and and_51 (and_51_out, ~in3, ~in2, ~in1, in0);  // And
  and and_52 (and_52_out, ~in3, ~in2, in1, ~in0);  // And
  and and_53 (and_53_out, ~in3, ~in2, in1, in0);  // And
  and and_54 (and_54_out, ~in3, in2, ~in1, ~in0);  // And
  and and_55 (and_55_out, ~in3, in2, in1, in0);  // And
  and and_56 (and_56_out, in3, ~in2, ~in1, in0);  // And
  and and_57 (and_57_out, in3, ~in2, ~in1, ~in0);  // And
  and and_58 (and_58_out, in3, ~in2, in1, ~in0);  // And
  and and_59 (and_59_out, in3, ~in2, in1, in0);  // And
  and and_60 (and_60_out, in3, in2, in1, ~in0);  // And
  and and_61 (and_61_out, in3, in2, in1, in0);
  or or_6 (seg_b, and_50_out, and_56_out, and_51_out, and_57_out, and_52_out, and_58_out, and_53_out, and_59_out, and_54_out, and_60_out, and_55_out, and_61_out);
  and and_62 (and_62_out, ~in3, ~in2, ~in1, ~in0);  // And
  and and_63 (and_63_out, ~in3, ~in2, in1, ~in0);  // And
  and and_64 (and_64_out, ~in3, ~in2, in1, in0);  // And
  and and_65 (and_65_out, ~in3, in2, ~in1, in0);  // And
  and and_66 (and_66_out, ~in3, in2, in1, ~in0);  // And
  and and_67 (and_67_out, ~in3, in2, in1, in0);  // And
  and and_68 (and_68_out, in3, ~in2, ~in1, in0);  // And
  and and_69 (and_69_out, in3, ~in2, in1, ~in0);  // And
  and and_70 (and_70_out, in3, in2, ~in1, ~in0);  // And
  and and_71 (and_71_out, in3, in2, ~in1, in0);  // And
  and and_72 (and_72_out, in3, in2, in1, ~in0);  // And
  and and_73 (and_73_out, in3, in2, in1, in0);
  or or_7 (seg_a, and_62_out, and_68_out, and_63_out, and_69_out, and_64_out, and_70_out, and_65_out, and_71_out, and_66_out, and_72_out, and_67_out, and_73_out);
  Seven_Seg seven_seg_1 (.a(1'b0), .b(1'b0), .c(1'b0), .d(1'b0), .e(1'b0), .f(1'b0), .g(in3), .dp(1'b0));
  Seven_Seg seven_seg_2 (.a(seg_a), .b(seg_b), .c(seg_c), .d(seg_d), .e(seg_e), .f(seg_f), .g(seg_g), .dp(1'b0));

  assign seg_dp = 1'b0;
  assign sign_a = 1'b0;
  assign sign_b = 1'b0;
  assign sign_c = 1'b0;
  assign sign_d = 1'b0;
  assign sign_dp = 1'b0;
  assign sign_e = 1'b0;
  assign sign_f = 1'b0;
  assign sign_g = in3;

  // Notes on the sheet:
  //   2
  //   3
  //   4
  //   5
  //   6
  //   -2
  //   -3
  //   -4
  //   -5
  //   -6
  //   -8
  //   0
  //   1
  //   7
  //   -1
  //   -7
  //   Interface (do not edit the content inside this box)
  //   Outputs:
  //   Inputs
  //   Sign
  //   Decimal Number
endmodule

/* Test case:
in3 in2 in1 in0  sign_a sign_b sign_c sign_d sign_e sign_f sign_g  seg_a seg_b seg_c seg_d seg_e seg_f seg_g
 0   0   0   0    0      0      0      0      0      0      0       1     1     1     1     1     1     0
*/
